# Fritzing sketch Wiring2 (saved by Fritzing 0.9.3b)

parts:
  Деталь1 = Arduino Nano (Rev3.0)
  S1 = H-Bridge with L298N
  M1 = DC Motor
  VCC1 = 4 x AAA Battery Mount
  Деталь2 = Bluetooth HC-05 Macho
  J1 = Basic Servo

nets:
  N1: Деталь1.D1/TX, Деталь2.RXD
  N2: Деталь1.D0/RX, Деталь2.TXD
  N3: Деталь1.D3, S1.ENB
  N4: Деталь1.D4, S1.IN4
  N5: Деталь1.D5, S1.IN3
  N6: Деталь1.D6, S1.IN2
  N7: Деталь1.D7, S1.IN1
  N8: Деталь1.D9, S1.ENA
  GND: Деталь1.GND, J1.gnd
  5V: Деталь1.5V, S1.5V, J1.vcc
  N9: S1.12V, VCC1.+
  N10: S1.GND, VCC1.-
  N11: S1.M1-01, S1.M2-02, M1.pin_1
  N12: S1.M1-02, S1.M2-01, M1.pin_2

custom parts:
  H-Bridge with L298N: h-bridge
