# Fritzing sketch Wiring (saved by Fritzing 0.9.2b)

parts:
  Part1 = Arduino Pro Mini v13
  J1 = Basic Servo
  S1 = Toggle Switch [package=THT]
  U1 = LIPO-2000mAh [package=lipo-2000]
  M2 = ESC
  920KV_Motor2 = DJI 920 KV Motor
  NRF24L2 = NRF24L01
  NRF24L3 = NRF24L01  # not connected
  U2 = Voltage Regulator - 3.3V [package="TO220 [THT]"]

nets:
  N1: Part1.VCC, M2.pin_8
  GND: Part1.GND, M2.GND
  N2: Part1.D13/SCK, NRF24L2.SCK
  N3: Part1.D12/MISO, NRF24L2.MISO
  N4: Part1.D11_PWM/MOSI, NRF24L2.MOSI
  N5: Part1.D10_PWM/SS, NRF24L2.CSN
  N6: Part1.D9_PWM, NRF24L2.CE
  N7: Part1.D2, M2.DATA
  GND_2: J1.gnd, NRF24L2.GND
  N8: S1.L2, U1.+
  N9: M2.U, 920KV_Motor2.w
  N10: M2.V, 920KV_Motor2.v
  N11: M2.W, 920KV_Motor2.u
  N12: NRF24L2.VCC, U2.output_voltage

notes:
  GND = Black
  VCC = Red
  CE = Yellow
  CSN = Green
  SCK = Orange
  MOSI = White
  MISO = Brown
  IRQ = Not Connected
  3.3v regulator or use the base breakout board of NRF24l01

custom parts:
  DJI 920 KV Motor: DJI Brushless Outrunner 2212/920K Motor F330-550
  NRF24L01: NRF24L01 module
