# Fritzing sketch Wiring1 (saved by Fritzing 0.9.2b)

parts:
  Part1 = Arduino Pro Mini v13
  Part2 = Power Cell LiPo Charger/Booster
  Part3 = Thumb Joystick
  Part4 = Thumb Joystick
  U1 = LIPO-1000mAh [package=lipo-1000]
  S1 = Toggle Switch [package=THT]
  NRF24L4 = NRF24L01  # not connected
  NRF24L5 = NRF24L01
  U2 = Voltage Regulator [package=to220-adj]

nets:
  VCC: Part1.VCC, Part3.VCC, Part4.VCC, S1.COM, U2.ADJ
  GND: Part1.GND, Part2.GND, Part3.GND, Part4.GND, U1.-, NRF24L5.GND
  N1: Part1.A1, Part4.HORZ
  N2: Part1.A0, Part3.VERT
  N3: Part1.D13/SCK, NRF24L5.SCK
  N4: Part1.D12/MISO, NRF24L5.MOSI
  N5: Part1.D11_PWM/MOSI, NRF24L5.MISO
  N6: Part1.D10_PWM/SS, NRF24L5.CSN
  N7: Part1.D9_PWM, NRF24L5.CE
  N8: Part2.VCC, S1.L2
  N9: Part2.5VIN, U1.+
  N10: NRF24L5.VCC, U2.OUT

notes:
  Trottle
  steering
  GND = Black
  VCC = Red
  CE = Yellow
  CSN = Green
  SCK = Orange
  MOSI = White
  MISO = Brown
  IRQ = Not Connected
  TP4056

custom parts:
  NRF24L01: NRF24L01 module
